# Fritzing sketch schematic_arduino_uno (saved by Fritzing 0.9.2b)
breadboards: 1

parts:
  Parte1 = Arduino Uno (Rev3)
  U1 = G3VM-61E1 [package=g3vm-61e1]
  LED1 = LED - 3mm [color="Red (633nm)" package="3 mm [THT]"]
  IR1 = TSOP312.., 314.. [package=THT]

nets:
  N1: Parte1.D11_PWM/MOSI, IR1.GND
  N2: Parte1.D12/MISO, U1.P$6
  N3: Parte1.3V3, LED1.anode, IR1.Data
  N4: Parte1.GND, U1.P$1, U1.P$5, IR1.Vs
  N5: U1.P$4, LED1.cathode
